// Digital circuit PC_ROM_SPLITTER_4_REGS.dig as structural Verilog
module PC_ROM_SPLITTER_4_REGS (
  input  clk,
  input  PC_RESET,
  output [9:0] CUR_INST_DATA,
  output [7:0] out_4,
  output [7:0] out_5,
  output [7:0] out_6,
  output [7:0] out_7,
  output [1:0] out_8
);

  wire decoder_1_out_0, decoder_1_out_1, decoder_1_out_2, decoder_1_out_3;
  wire [7:0] PC_out;

  Counter #(.Bits(8)) PC (.en(clk), .C(clk), .clr(PC_RESET), .out(PC_out));  // open: ovf
  ROM #(.AddrBits(8), .Bits(10)) INSTR_MEM (.A(PC_out), .sel(1'b1), .D(CUR_INST_DATA));
  Decoder #(.Selector_Bits(2)) decoder_1 (
    .sel(CUR_INST_DATA[1:0]), .out_0(decoder_1_out_0), .out_1(decoder_1_out_1), .out_2(decoder_1_out_2),
    .out_3(decoder_1_out_3));
  Register #(.Bits(8)) register_1 (.D(CUR_INST_DATA[9:2]), .C(clk), .en(decoder_1_out_0), .Q(out_4));
  Register #(.Bits(8)) register_2 (.D(CUR_INST_DATA[9:2]), .C(clk), .en(decoder_1_out_1), .Q(out_5));
  Register #(.Bits(8)) register_3 (.D(CUR_INST_DATA[9:2]), .C(clk), .en(decoder_1_out_2), .Q(out_6));
  Register #(.Bits(8)) register_4 (.D(CUR_INST_DATA[9:2]), .C(clk), .en(decoder_1_out_3), .Q(out_7));

  assign out_8 = CUR_INST_DATA[1:0];

  // Other names for the same wires on the sheet: c = clk; reset = PC_RESET

  // Notes on the sheet:
  //   contents of INSTR_MEM (hex, n*v repeats v):
  //   7,5,6,14
endmodule
